# Fritzing sketch 2Out_Headphone_Amp (saved by Fritzing 0.9.0b)
breadboards: 1

parts:
  IC1 = Dual Op-Amp [package=dip08]
  IC2 = Dual Op-Amp [package=dip08]
  IC3 = Dual Op-Amp [package=dip08]
  C1 = Tantalum Capacitor [capacitance=1μF package="100 mil [THT, tantalum]"]
  R1 = Resistor [tolerance=±5% resistance=100k package=THT]
  R2 = TRIMPOT [package=trimpot_pth_s3_lock]
  J1 = female pin header, 1 pin [form="♀ (female)"]
  R3 = Resistor [tolerance=±5% resistance=2.2k package=THT]
  R4 = Resistor [tolerance=±5% resistance=1k package=THT]
  J2 = female pin header, 1 pin [form="♀ (female)"]
  J3 = female pin header, 1 pin [form="♀ (female)"]
  C2 = Electrolytic Capacitor [capacitance=0.22mF package="100 mil [THT, electrolytic]"]
  C3 = Electrolytic Capacitor [capacitance=1µF package="100 mil [THT, electrolytic]"]  # not connected

nets:
  N1: IC1.A_OUT, IC2.A_+IN, IC3.A_+IN, R3.Pin_1
  N2: IC1.A_-IN, R3.Pin_0, R4.Pin_0
  N3: IC1.A_+IN, C1.+, R1.Pin_0
  N4: IC1.A_V-, IC2.A_V-, IC3.A_V-, R1.Pin_1, R2.CW, R4.Pin_1, C2.-
  N5: IC1.A_V+, IC2.A_V+, IC3.A_V+, C2.+
  N6: IC2.A_OUT, IC2.A_-IN, J2.pin1
  N7: IC3.A_OUT, IC3.A_-IN, J3.pin1
  N8: C1.-, R2.WIPER
  N9: R2.CCW, J1.pin1

notes:
  GND
  +3V
  -3V
  GND
